# Fritzing sketch Wiring_MARS (saved by Fritzing 0.9.9b)
breadboards: 1

parts:
  BAT1 = Battery Holders [package=battcon_20mm_4legs]
  M1 = RioRand LM2596
  S1 = Round Pushbutton
  Mod1 = Raspberry Pi 4B
  J1 = STM32 Nucleo boards
  U2 = MAX485 Breakout [chip_label=? package=THT]
  U7 = Molex Picoblade Series Header [part_number=0533980471 package=Picoblade-53398-0471]
  U8 = Molex Picoblade Series Header [part_number=0533980471 package=Picoblade-53398-0471]
  U9 = Molex Picoblade Series Header [part_number=0533980471 package=Picoblade-53398-0471]
  U10 = Molex Picoblade Series Header [part_number=0533980471 package=Picoblade-53398-0471]
  U11 = Molex Picoblade Series Header [part_number=0533980471 package=Picoblade-53398-0471]
  U12 = Molex Picoblade Series Header [part_number=0533980471 package=Picoblade-53398-0471]
  U13 = Molex Picoblade Series Header [part_number=0533980471 package=Picoblade-53398-0471]
  U14 = Molex Picoblade Series Header [part_number=0533980471 package=Picoblade-53398-0471]
  U15 = MAX485 Breakout [chip_label=? package=THT]

nets:
  N1: BAT1.+, M1.Pin_2, S1.leg0, U7.2, U8.2, U9.2, U10.2, U11.2, U12.2, U13.2, U14.2
  N2: BAT1.-, M1.Pin_1, S1.leg1, U7.1, U8.1, U9.1, U10.1, U11.1, U12.1, U13.1, U14.1
  VCC: M1.Pin_3, J1.VIN, U2.VCC, U15.VCC
  GND: M1.Pin_4, J1.GND, U2.GND, U15.GND
  N3: Mod1.GPIO14, J1.PA9
  N4: Mod1.GPIO15, J1.PA10
  N5: Mod1.GPIO19, J1.D12/MISO
  N6: Mod1.GPIO20, J1.D11_PWM/MOSI
  N7: Mod1.GPIO21, J1.D13/SCK
  N8: J1.PB11, U2.RO
  N9: J1.PB10, U2.DI
  N10: J1.PA2, U15.DI
  N11: J1.PA3, U15.RO
  N12: J1.PA0, U2.RE, U2.DE
  N13: J1.PA1, U15.RE, U15.DE
  N14: U2.B, U11.4, U12.4, U13.4, U14.4
  N15: U2.A, U11.3, U12.3, U13.3, U14.3
  N16: U7.3, U8.3, U9.3, U10.3, U15.B
  N17: U7.4, U8.4, U9.4, U10.4, U15.A

custom parts:
  MAX485 Breakout: MAX485 RS485 breakout board
